// Logisim project logism circuit file.circ as structural Verilog: 1 circuit, main circuit main
module main (
  input  clk,
  output NS_Red,
  output EW_Yellow,
  output EW_Green,
  output NS_Green,
  output NS_Yellow,
  output EW_Red
);

  wire and_1_out, d_ff_1_q, d_ff_1_qn, d_ff_2_q, d_ff_2_qn, not_1_out;

  D_Flip_Flop d_ff_1 (.clk(d_ff_1_qn), .D(clk), .Q(d_ff_1_q), .Qn(d_ff_1_qn));  // open: preset, en, reset
  D_Flip_Flop d_ff_2 (.clk(d_ff_2_qn), .D(d_ff_1_qn), .Q(d_ff_2_q), .Qn(d_ff_2_qn));  // open: preset, en, reset
  D_Flip_Flop d_ff_3 (.clk(EW_Red), .D(d_ff_2_qn), .Q(NS_Red), .Qn(EW_Red));  // open: preset, en, reset
  and and_1 (and_1_out, d_ff_1_q, d_ff_2_q);
  not not_1 (not_1_out, and_1_out);
  and and_2 (EW_Yellow, NS_Red, and_1_out);
  and and_3 (EW_Green, NS_Red, not_1_out);
  and and_4 (NS_Green, not_1_out, EW_Red);
  and and_5 (NS_Yellow, and_1_out, EW_Red);

  // Notes on the sheet:
  //   Inputs: clk
  //   Traffic Signal Controller (2-way, 8-step cycle)
  //   Count 0-2: NS Green / EW Red | 3: NS Yellow | 4-6: EW Green / NS Red | 7: EW Yellow
  //   Toggle clk with the Poke tool: each 0 to 1 edge advances one step (8 steps per cycle).
  //   Outputs
endmodule
